// Logisim project 8-bit_computer.circ as structural Verilog: 8 circuits, main circuit Memory cell
module main (
  input  Counter_OE,
  input  Count_Enable,
  input  OE,
  input  [7:0] Testing_Data_Inputs,
  input  WE,
  input  [3:0] OE_Testing_Data,
  input  OE_Testing_Data_2,
  input  OE_2,
  input  Internal_OE,
  input  WE_2,
  input  OE_3,
  input  WE_3,
  input  WE_4,
  input  OE_4,
  input  OE_5,
  input  WE_5,
  input  Cin,
  input  [2:0] in_18,
  input  WE_6,
  input  Sub,
  input  OE_6,
  input  OE_7,
  input  WE_7,
  output [3:0] MAR_content,
  output [3:0] Counter_Content,
  output [7:0] IR_content,
  output [7:0] MBR_Content,
  output [7:0] Reg_A_content,
  output [7:0] ALU_Result,
  output out_30,
  output [7:0] OR_content,
  output [7:0] Reg_B_content,
  output Cout
);

  wire Clock_out;
  wire [3:0] controlled_buffer_1_out, MAR_dout;
  wire [7:0] alu_modified_8bits_1_out_8, bit_extender_1_out, Instruction_register_dout;
  wire [31:0] Dec__Decoder_2_dout, Dec__Decoder_3_dout, Dec__Decoder_4_dout, Dec__Decoder_5_dout,
       Dec__Decoder_dout;

  Clock Clock (.out(Clock_out));
  Counter #(.width(4), .max('h3)) PC (
    .D(controlled_buffer_1_out), .count(Count_Enable), .Q(Counter_Content), .clk(Clock_out));  // open: load, carry, clr
  Registers Instruction_register (
    .Clock(Clock_out), .WE(WE_2), .Din(alu_modified_8bits_1_out_8), .OE(OE_3),
    .Dout(Instruction_register_dout), .Stored_Data(IR_content));
  assign controlled_buffer_1_out = Counter_OE ? Counter_Content : 4'bz;  // Controlled_Buffer controlled_buffer_1
  Decimal_Decoder Dec__Decoder (.Din(Reg_A_content), .Dout(Dec__Decoder_dout));
  Registers Reg_A (
    .Clock(Clock_out), .WE(WE_5), .Din(alu_modified_8bits_1_out_8), .Stored_Data(Reg_A_content));  // open: OE, Dout
  ALU_modified_8bits alu_modified_8bits_1 (
    .Select(in_18), .sub(Sub), .A(Reg_A_content), .B(Reg_B_content), .out_8(alu_modified_8bits_1_out_8),
    .Zero(out_30), .OE(OE_7), .Cout(Cout), .Cin(Cin), .out_7(ALU_Result));
  Registers Reg_B (
    .Clock(Clock_out), .WE(WE_7), .Din(alu_modified_8bits_1_out_8), .Stored_Data(Reg_B_content));  // open: OE, Dout
  Decimal_Decoder Dec__Decoder_2 (.Din(Reg_B_content), .Dout(Dec__Decoder_2_dout));
  _7_Segment_Display u_7_segment_display_1 (
    .g(Dec__Decoder_dout[15]), .f(Dec__Decoder_dout[14]), .a(Dec__Decoder_dout[13]),
    .b(Dec__Decoder_dout[12]), .e(Dec__Decoder_dout[31]), .d(Dec__Decoder_dout[30]),
    .c(Dec__Decoder_dout[29]), .dp(Dec__Decoder_dout[28]));
  _7_Segment_Display u_7_segment_display_2 (
    .g(Dec__Decoder_2_dout[15]), .f(Dec__Decoder_2_dout[14]), .a(Dec__Decoder_2_dout[13]),
    .b(Dec__Decoder_2_dout[12]), .e(Dec__Decoder_2_dout[31]), .d(Dec__Decoder_2_dout[30]),
    .c(Dec__Decoder_2_dout[29]), .dp(Dec__Decoder_2_dout[28]));
  assign bit_extender_1_out = {{4{1'b0}}, Counter_Content};  // Bit_Extender bit_extender_1
  Decimal_Decoder Dec__Decoder_3 (.Din(bit_extender_1_out), .Dout(Dec__Decoder_3_dout));
  _7_Segment_Display u_7_segment_display_3 (
    .g(Dec__Decoder_dout[11]), .f(Dec__Decoder_dout[10]), .a(Dec__Decoder_dout[9]), .b(Dec__Decoder_dout[8]),
    .e(Dec__Decoder_dout[27]), .d(Dec__Decoder_dout[26]), .c(Dec__Decoder_dout[25]),
    .dp(Dec__Decoder_dout[24]));
  _7_Segment_Display u_7_segment_display_4 (
    .g(Dec__Decoder_dout[7]), .f(Dec__Decoder_dout[6]), .a(Dec__Decoder_dout[5]), .b(Dec__Decoder_dout[4]),
    .e(Dec__Decoder_dout[23]), .d(Dec__Decoder_dout[22]), .c(Dec__Decoder_dout[21]),
    .dp(Dec__Decoder_dout[20]));
  _7_Segment_Display u_7_segment_display_5 (
    .g(Dec__Decoder_2_dout[11]), .f(Dec__Decoder_2_dout[10]), .a(Dec__Decoder_2_dout[9]),
    .b(Dec__Decoder_2_dout[8]), .e(Dec__Decoder_2_dout[27]), .d(Dec__Decoder_2_dout[26]),
    .c(Dec__Decoder_2_dout[25]), .dp(Dec__Decoder_2_dout[24]));
  _7_Segment_Display u_7_segment_display_6 (
    .g(Dec__Decoder_2_dout[7]), .f(Dec__Decoder_2_dout[6]), .a(Dec__Decoder_2_dout[5]),
    .b(Dec__Decoder_2_dout[4]), .e(Dec__Decoder_2_dout[23]), .d(Dec__Decoder_2_dout[22]),
    .c(Dec__Decoder_2_dout[21]), .dp(Dec__Decoder_2_dout[20]));
  _7_Segment_Display u_7_segment_display_7 (
    .g(Dec__Decoder_3_dout[3]), .f(Dec__Decoder_3_dout[2]), .a(Dec__Decoder_3_dout[1]),
    .b(Dec__Decoder_3_dout[0]), .e(Dec__Decoder_3_dout[19]), .d(Dec__Decoder_3_dout[18]),
    .c(Dec__Decoder_3_dout[17]), .dp(Dec__Decoder_3_dout[16]));
  _7_Segment_Display u_7_segment_display_8 (
    .g(Dec__Decoder_dout[3]), .f(Dec__Decoder_dout[2]), .a(Dec__Decoder_dout[1]), .b(Dec__Decoder_dout[0]),
    .e(Dec__Decoder_dout[19]), .d(Dec__Decoder_dout[18]), .c(Dec__Decoder_dout[17]),
    .dp(Dec__Decoder_dout[16]));
  _7_Segment_Display u_7_segment_display_9 (
    .g(Dec__Decoder_2_dout[3]), .f(Dec__Decoder_2_dout[2]), .a(Dec__Decoder_2_dout[1]),
    .b(Dec__Decoder_2_dout[0]), .e(Dec__Decoder_2_dout[19]), .d(Dec__Decoder_2_dout[18]),
    .c(Dec__Decoder_2_dout[17]), .dp(Dec__Decoder_2_dout[16]));
  BitSelector #(.group(4)) bitselector_1 (.in(Instruction_register_dout), .out(controlled_buffer_1_out), .sel(1'b0));
  LED D6 (.in(alu_modified_8bits_1_out_8[6]));
  LED D7 (.in(alu_modified_8bits_1_out_8[7]));
  LED D5 (.in(alu_modified_8bits_1_out_8[5]));
  assign alu_modified_8bits_1_out_8 = OE_Testing_Data_2 ? Testing_Data_Inputs : 8'bz;  // Controlled_Buffer controlled_buffer_2
  LED D2 (.in(alu_modified_8bits_1_out_8[2]));
  LED D4 (.in(alu_modified_8bits_1_out_8[4]));
  LED D1 (.in(alu_modified_8bits_1_out_8[1]));
  LED D3 (.in(alu_modified_8bits_1_out_8[3]));
  LED D0 (.in(alu_modified_8bits_1_out_8[0]));
  MAR MAR (
    .Clock(Clock_out), .WE(WE), .Din(controlled_buffer_1_out), .OE(OE_2), .Dout(MAR_dout),
    .Stored_Data(MAR_content));
  assign alu_modified_8bits_1_out_8 = Internal_OE ? MBR_Content : 8'bz;  // Controlled_Buffer controlled_buffer_3
  Registers MBR (
    .Clock(Clock_out), .WE(WE_3), .Din(alu_modified_8bits_1_out_8), .OE(OE_4),
    .Dout(alu_modified_8bits_1_out_8), .Stored_Data(MBR_Content));
  Registers Output_Registers (
    .Clock(Clock_out), .WE(WE_6), .Din(alu_modified_8bits_1_out_8), .OE(OE_6),
    .Dout(alu_modified_8bits_1_out_8), .Stored_Data(OR_content));
  Decimal_Decoder Dec__Decoder_4 (.Din(OR_content), .Dout(Dec__Decoder_4_dout));
  assign MAR_dout = OE ? OE_Testing_Data : 4'bz;  // Controlled_Buffer controlled_buffer_4
  _7_Segment_Display u_7_segment_display_10 (
    .g(Dec__Decoder_4_dout[15]), .f(Dec__Decoder_4_dout[14]), .a(Dec__Decoder_4_dout[13]),
    .b(Dec__Decoder_4_dout[12]), .e(Dec__Decoder_4_dout[31]), .d(Dec__Decoder_4_dout[30]),
    .c(Dec__Decoder_4_dout[29]), .dp(Dec__Decoder_4_dout[28]));
  _7_Segment_Display u_7_segment_display_11 (
    .g(Dec__Decoder_4_dout[11]), .f(Dec__Decoder_4_dout[10]), .a(Dec__Decoder_4_dout[9]),
    .b(Dec__Decoder_4_dout[8]), .e(Dec__Decoder_4_dout[27]), .d(Dec__Decoder_4_dout[26]),
    .c(Dec__Decoder_4_dout[25]), .dp(Dec__Decoder_4_dout[24]));
  _7_Segment_Display u_7_segment_display_12 (
    .g(Dec__Decoder_4_dout[3]), .f(Dec__Decoder_4_dout[2]), .a(Dec__Decoder_4_dout[1]),
    .b(Dec__Decoder_4_dout[0]), .e(Dec__Decoder_4_dout[19]), .d(Dec__Decoder_4_dout[18]),
    .c(Dec__Decoder_4_dout[17]), .dp(Dec__Decoder_4_dout[16]));
  _7_Segment_Display u_7_segment_display_13 (
    .g(Dec__Decoder_4_dout[7]), .f(Dec__Decoder_4_dout[6]), .a(Dec__Decoder_4_dout[5]),
    .b(Dec__Decoder_4_dout[4]), .e(Dec__Decoder_4_dout[23]), .d(Dec__Decoder_4_dout[22]),
    .c(Dec__Decoder_4_dout[21]), .dp(Dec__Decoder_4_dout[20]));
  LED D7_2 (.in(alu_modified_8bits_1_out_8[7]));
  LED D6_2 (.in(alu_modified_8bits_1_out_8[6]));
  LED D5_2 (.in(alu_modified_8bits_1_out_8[5]));
  LED D2_2 (.in(alu_modified_8bits_1_out_8[2]));
  LED D3_2 (.in(alu_modified_8bits_1_out_8[3]));
  LED D1_2 (.in(alu_modified_8bits_1_out_8[1]));
  LED D4_2 (.in(alu_modified_8bits_1_out_8[4]));
  LED D0_2 (.in(alu_modified_8bits_1_out_8[0]));
  Decimal_Decoder Dec__Decoder_5 (.Dout(Dec__Decoder_5_dout));  // open: Din
  RAM #(.addrWidth(4), .bus("separate")) ram_1 (
    .addr(MAR_dout), .din(alu_modified_8bits_1_out_8), .data(alu_modified_8bits_1_out_8), .str(WE_4),
    .clk(Clock_out), .ld(OE_5));  // open: sel, clr
  _7_Segment_Display u_7_segment_display_14 (
    .g(Dec__Decoder_5_dout[15]), .f(Dec__Decoder_5_dout[14]), .a(Dec__Decoder_5_dout[13]),
    .b(Dec__Decoder_5_dout[12]), .e(Dec__Decoder_5_dout[31]), .d(Dec__Decoder_5_dout[30]),
    .c(Dec__Decoder_5_dout[29]), .dp(Dec__Decoder_5_dout[28]));
  _7_Segment_Display u_7_segment_display_15 (
    .g(Dec__Decoder_5_dout[11]), .f(Dec__Decoder_5_dout[10]), .a(Dec__Decoder_5_dout[9]),
    .b(Dec__Decoder_5_dout[8]), .e(Dec__Decoder_5_dout[27]), .d(Dec__Decoder_5_dout[26]),
    .c(Dec__Decoder_5_dout[25]), .dp(Dec__Decoder_5_dout[24]));
  _7_Segment_Display u_7_segment_display_16 (
    .g(Dec__Decoder_5_dout[7]), .f(Dec__Decoder_5_dout[6]), .a(Dec__Decoder_5_dout[5]),
    .b(Dec__Decoder_5_dout[4]), .e(Dec__Decoder_5_dout[23]), .d(Dec__Decoder_5_dout[22]),
    .c(Dec__Decoder_5_dout[21]), .dp(Dec__Decoder_5_dout[20]));
  _7_Segment_Display u_7_segment_display_17 (
    .g(Dec__Decoder_5_dout[3]), .f(Dec__Decoder_5_dout[2]), .a(Dec__Decoder_5_dout[1]),
    .b(Dec__Decoder_5_dout[0]), .e(Dec__Decoder_5_dout[19]), .d(Dec__Decoder_5_dout[18]),
    .c(Dec__Decoder_5_dout[17]), .dp(Dec__Decoder_5_dout[16]));

  // Notes on the sheet:
  //   Internal Address Bus
  //   Internal Data Bus
  //   External Address Bus
  //   External Data Bus
endmodule

module Memory_cell (
  input  Clock,
  input  WE,
  input  Din,
  input  OE,
  input  Reset,
  output Dout,
  output Stored_Data
);

  wire and_1_out, and_2_out, not_1_out, or_1_out;

  not not_1 (not_1_out, WE);
  and and_1 (and_1_out, Stored_Data, not_1_out);
  and and_2 (and_2_out, WE, Din);
  or or_1 (or_1_out, and_1_out, and_2_out);
  D_Flip_Flop d_ff_1 (.clk(Clock), .D(or_1_out), .Q(Stored_Data), .reset(Reset));  // open: Qn, preset, en
  assign Dout = OE ? Stored_Data : 1'bz;  // Controlled_Buffer controlled_buffer_1

  // Notes on the sheet:
  //   Memory Cell
endmodule

module Registers (
  input  Clock,
  input  WE,
  input  [7:0] Din,
  input  OE,
  output [7:0] Dout,
  output [7:0] Stored_Data
);

  Memory_cell _0 (
    .Clock(Clock), .WE(WE), .Din(Din[0]), .OE(OE), .Dout(Dout[0]), .Stored_Data(Stored_Data[0]));  // open: Reset
  Memory_cell _1 (
    .Clock(Clock), .WE(WE), .Din(Din[1]), .OE(OE), .Dout(Dout[1]), .Stored_Data(Stored_Data[1]));  // open: Reset
  Memory_cell _2 (
    .Clock(Clock), .WE(WE), .Din(Din[2]), .OE(OE), .Dout(Dout[2]), .Stored_Data(Stored_Data[2]));  // open: Reset
  Memory_cell _3 (
    .Clock(Clock), .WE(WE), .Din(Din[3]), .OE(OE), .Dout(Dout[3]), .Stored_Data(Stored_Data[3]));  // open: Reset
  Memory_cell _5 (
    .Clock(Clock), .WE(WE), .Din(Din[4]), .OE(OE), .Dout(Dout[4]), .Stored_Data(Stored_Data[4]));  // open: Reset
  Memory_cell _5_2 (
    .Clock(Clock), .WE(WE), .Din(Din[5]), .OE(OE), .Dout(Dout[5]), .Stored_Data(Stored_Data[5]));  // open: Reset
  Memory_cell _6 (
    .Clock(Clock), .WE(WE), .Din(Din[6]), .OE(OE), .Dout(Dout[6]), .Stored_Data(Stored_Data[6]));  // open: Reset
  Memory_cell _7 (
    .Clock(Clock), .WE(WE), .Din(Din[7]), .OE(OE), .Dout(Dout[7]), .Stored_Data(Stored_Data[7]));  // open: Reset

  // Notes on the sheet:
  //   Register(8 bits)
endmodule

module MAR (
  input  Clock,
  input  WE,
  input  [3:0] Din,
  input  OE,
  output [3:0] Dout,
  output [3:0] Stored_Data
);

  Memory_cell _0 (
    .Clock(Clock), .WE(WE), .Din(Din[0]), .OE(OE), .Dout(Dout[0]), .Stored_Data(Stored_Data[0]));  // open: Reset
  Memory_cell _1 (
    .Clock(Clock), .WE(WE), .Din(Din[1]), .OE(OE), .Dout(Dout[1]), .Stored_Data(Stored_Data[1]));  // open: Reset
  Memory_cell _2 (
    .Clock(Clock), .WE(WE), .Din(Din[2]), .OE(OE), .Dout(Dout[2]), .Stored_Data(Stored_Data[2]));  // open: Reset
  Memory_cell _3 (
    .Clock(Clock), .WE(WE), .Din(Din[3]), .OE(OE), .Dout(Dout[3]), .Stored_Data(Stored_Data[3]));  // open: Reset

  // Notes on the sheet:
  //   Register(8 bits)
endmodule

module ALU (
  input  [7:0] Reg_A,
  input  [7:0] Reg_B,
  input  OE,
  output [7:0] Dout,
  output [7:0] ALU_Result,
  output Carry_Out
);

  Adder adder_1 (.a(Reg_A), .b(Reg_B), .out(ALU_Result), .cout(Carry_Out));  // open: cin
  assign Dout = OE ? ALU_Result : 8'bz;  // Controlled_Buffer controlled_buffer_1
endmodule

module Decimal_Decoder (
  input  [7:0] Din,
  output [31:0] Dout
);

  ROM #(.dataWidth(32)) rom_1 (
    .addr(Din),
    .data({Dout[31:28], Dout[15:12], Dout[27:24], Dout[11:8], Dout[23:20], Dout[7:4], Dout[19:16], Dout[3:0]}));  // open: sel

  // Notes on the sheet:
  //   Decimal Decoder
  //   contents of rom_1 (hex, n*v repeats v):
  //   e7 21 cb 6b 2d 6e ee 23 ef 2f 21e7 2121 21cb 216b 212d 216e 21ee 2123 21ef 212f cbe7 cb21 cbcb cb6b
  //   cb2d cb6e cbee cb23 cbef cb2f 6be7 6b21 6bcb 6b6b 6b2d 6b6e 6bee 6b23 6bef 6b2f 2de7 2d21 2dcb 2d6b
  //   2d2d 2d6e 2dee 2d23 2def 2d2f 6ee7 6e21 6ecb 6e6b 6e2d 6e6e 6eee 6e23 6eef 6e2f eee7 ee21 eecb ee6b
  //   ee2d ee6e eeee ee23 eeef ee2f 23e7 2321 23cb 236b 232d 236e 23ee 2323 23ef 232f efe7 ef21 efcb ef6b
  //   ef2d ef6e efee ef23 efef ef2f 2fe7 2f21 2fcb 2f6b 2f2d 2f6e 2fee 2f23 2fef 2f2f 21e7e7 21e721 21e7cb
  //   21e76b 21e72d 21e76e 21e7ee 21e723 21e7ef 21e72f 2121e7 212121 2121cb 21216b 21212d 21216e 2121ee
  //   212123 2121ef 21212f 21cbe7 21cb21 21cbcb 21cb6b 21cb2d 21cb6e 21cbee 21cb23 21cbef 21cb2f 216be7
  //   216b21 216bcb 216b6b 216b2d 216b6e 216bee 216b23 216bef 216b2f 212de7 212d21 212dcb 212d6b 212d2d
  //   212d6e 212dee 212d23 212def 212d2f 216ee7 216e21 216ecb 216e6b 216e2d 216e6e 216eee 216e23 216eef
  //   216e2f 21eee7 21ee21 21eecb 21ee6b 21ee2d 21ee6e 21eeee 21ee23 21eeef 21ee2f 2123e7 212321 2123cb
  //   21236b 21232d 21236e 2123ee 212323 2123ef 21232f 21efe7 21ef21 21efcb 21ef6b 21ef2d 21ef6e 21efee
  //   21ef23 21efef 21ef2f 212fe7 212f21 212fcb 212f6b 212f2d 212f6e 212fee 212f23 212fef 212f2f cbe7e7
  //   cbe721 cbe7cb cbe76b cbe72d cbe76e cbe7ee cbe723 cbe7ef cbe72f cb21e7 cb2121 cb21cb cb216b cb212d
  //   cb216e cb21ee cb2123 cb21ef cb212f cbcbe7 cbcb21 cbcbcb cbcb6b cbcb2d cbcb6e cbcbee cbcb23 cbcbef
  //   cbcb2f cb6be7 cb6b21 cb6bcb cb6b6b cb6b2d cb6b6e cb6bee cb6b23 cb6bef cb6b2f cb2de7 cb2d21 cb2dcb
  //   cb2d6b cb2d2d cb2d6e cb2dee cb2d23 cb2def cb2d2f cb6ee7 cb6e21 cb6ecb cb6e6b cb6e2d cb6e6e
endmodule

module ALU_modifited (
  input  sub,
  input  Cin,
  input  [2:0] in_3,
  input  A,
  input  B,
  output out_6,
  output out_7
);

  wire adder_1_out, and_1_out, nor_1_out, or_1_out, xor_1_out, xor_2_out;

  xor xor_1 (xor_1_out, B, sub);
  and and_1 (and_1_out, A, B);
  or or_1 (or_1_out, A, B);
  xor xor_2 (xor_2_out, A, B);
  nor nor_1 (nor_1_out, A, B);
  Adder #(.width(1)) adder_1 (.a(A), .b(xor_1_out), .out(adder_1_out), .cin(Cin), .cout(out_7));
  Multiplexer #(.select(3), .enable("false")) multiplexer_1 (
    .in0(and_1_out), .in1(or_1_out), .in2(xor_2_out), .in3(nor_1_out), .in4(adder_1_out), .out(out_6),
    .sel(in_3));  // open: in5, in6, in7
endmodule

module ALU_modified_8bits (
  input  [2:0] Select,
  input  sub,
  input  [7:0] A,
  input  Cin,
  input  [7:0] B,
  input  OE,
  output [7:0] out_7,
  output [7:0] out_8,
  output Zero,
  output Cout
);

  wire alu_modifited_1_out_7, alu_modifited_2_out_7, alu_modifited_3_out_7, alu_modifited_4_out_7,
       alu_modifited_5_out_7, alu_modifited_6_out_7, alu_modifited_7_out_7;

  ALU_modifited alu_modifited_1 (
    .A(A[0]), .B(B[0]), .out_6(out_7[0]), .sub(sub), .Cin(Cin), .in_3(Select), .out_7(alu_modifited_1_out_7));
  ALU_modifited alu_modifited_2 (
    .A(A[1]), .B(B[1]), .out_6(out_7[1]), .sub(sub), .Cin(alu_modifited_1_out_7), .in_3(Select),
    .out_7(alu_modifited_2_out_7));
  ALU_modifited alu_modifited_3 (
    .A(A[2]), .B(B[2]), .out_6(out_7[2]), .sub(sub), .Cin(alu_modifited_2_out_7), .in_3(Select),
    .out_7(alu_modifited_3_out_7));
  ALU_modifited alu_modifited_4 (
    .A(A[3]), .B(B[3]), .out_6(out_7[3]), .sub(sub), .Cin(alu_modifited_3_out_7), .in_3(Select),
    .out_7(alu_modifited_4_out_7));
  ALU_modifited alu_modifited_5 (
    .A(A[4]), .B(B[4]), .out_6(out_7[4]), .sub(sub), .Cin(alu_modifited_4_out_7), .in_3(Select),
    .out_7(alu_modifited_5_out_7));
  ALU_modifited alu_modifited_6 (
    .A(A[5]), .B(B[5]), .out_6(out_7[5]), .sub(sub), .Cin(alu_modifited_5_out_7), .in_3(Select),
    .out_7(alu_modifited_6_out_7));
  ALU_modifited alu_modifited_7 (
    .A(A[6]), .B(B[6]), .out_6(out_7[6]), .sub(sub), .Cin(alu_modifited_6_out_7), .in_3(Select),
    .out_7(alu_modifited_7_out_7));
  ALU_modifited alu_modifited_8 (
    .A(A[7]), .B(B[7]), .out_6(out_7[7]), .sub(sub), .Cin(alu_modifited_7_out_7), .in_3(Select), .out_7(Cout));
  nor nor_1 (Zero, out_7[0], out_7[1], out_7[2], out_7[3], out_7[4], out_7[5], out_7[6], out_7[7]);
  assign out_8 = OE ? out_7 : 8'bz;  // Controlled_Buffer controlled_buffer_1
endmodule
